# Fritzing sketch ULTFreezer-monitor-sparkfun (saved by Fritzing 0.9.4)
circuit board: 8.59307cm x 5.18096cm
breadboards: 1

parts:
  Amica_NodeMCU = NodeMCU V1.0
  PART1 = SparkFun MAX31855K Thermocouple Breakout [part_number=SEN-13266]
  J1 = Power Jack [package=power_jack_pth_lock]

nets:
  N1: Amica_NodeMCU.D1, PART1.SO
  3V3: Amica_NodeMCU.3V3, PART1.VCC
  GND: Amica_NodeMCU.GND, PART1.GND, J1.GND
  N2: Amica_NodeMCU.D6, PART1.SCK
  N3: Amica_NodeMCU.D7, PART1.CS
  N4: Amica_NodeMCU.Vin, J1.PWR

custom parts:
  NodeMCU V1.0: ESP8266 based NodeMCU
  SparkFun MAX31855K Thermocouple Breakout: The MAX31855K IC takes a standard k-type thermocouple in one end, digitizes the temperature measured and sends that data out the other end via SPI. For more information, please visit www.sparkfun.com
