# Fritzing sketch ultraLowFreezerMonitor (saved by Fritzing 0.9.4)
breadboards: 1

parts:
  U1 = NodeMCU V1.0
  PART1 = SparkFun MAX31855K Thermocouple Breakout [part_number=SEN-13266]

nets:
  N1: U1.D1, PART1.SCK
  N2: U1.D2, PART1.SO
  3V3: U1.3V3, PART1.VCC
  GND: U1.GND, PART1.GND
  N3: U1.D7, PART1.NC

custom parts:
  NodeMCU V1.0: ESP8266 based NodeMCU
  SparkFun MAX31855K Thermocouple Breakout: The MAX31855K IC takes a standard k-type thermocouple in one end, digitizes the temperature measured and sends that data out the other end via SPI. For more information, please visit www.sparkfun.com
